// Logisim project CLUSTER-1.circ as structural Verilog: 9 circuits, main circuit MAIN
module MAIN (
);

  wire BRANCH, control_1_alu_a_sel, control_1_clk, control_1_flash_wr, control_1_rst, control_1_sto,
       HALT_out, not_1_out, reg_file_1_wb_eq, WB_A, WB_B;
  wire [2:0] B_OP_S, control_1_alu_a_op, control_1_mode, decode_1_alu_a, decode_1_alu_b;
  wire [4:0] decode_1_sel_a, decode_1_sel_b, decode_1_sel_c, decode_1_sel_d, decode_1_wb_a, decode_1_wb_b;
  wire [7:0] alu_a_1_flags, B_FLAGS;
  wire [31:0] agu_bpu_1_pc_output, alu_a_1_results, alu_b_1_results, decode_1_instr_out, flash_1_data_out,
       multiplexer_1_out, multiplexer_2_out, multiplexer_3_out, ram_stack_1_data_out, reg_file_1_out_a,
       reg_file_1_out_b, reg_file_1_out_c, reg_file_1_out_d, reg_file_1_pc_output;

  Button HALT (.out(HALT_out));
  CONTROL control_1 (
    .CLK(control_1_clk), .RST(control_1_rst), .WB_EQ(reg_file_1_wb_eq), .ALU_A_SEL(control_1_alu_a_sel),
    .ALU_A_OP(control_1_alu_a_op), .ALU_A_FLAGS(alu_a_1_flags), .WB_A(WB_A), .WB_B(WB_B),
    .MODE(control_1_mode), .B_OP_S(B_OP_S), .B_FLAGS(B_FLAGS), .STO(control_1_sto), .BRANCH(BRANCH),
    .FLASH_WR(control_1_flash_wr), .HALT(HALT_out));
  DECODE decode_1 (
    .INSTR_IN(flash_1_data_out), .SEL_A(decode_1_sel_a), .SEL_B(decode_1_sel_b), .SEL_C(decode_1_sel_c),
    .SEL_D(decode_1_sel_d), .WB_A(decode_1_wb_a), .WB_B(decode_1_wb_b), .ALU_A(decode_1_alu_a),
    .ALU_B(decode_1_alu_b), .INSTR_OUT(decode_1_instr_out));
  not not_1 (not_1_out, control_1_alu_a_sel);
  ALU_A alu_a_1 (
    .B_INPUT(reg_file_1_out_b), .A_INPUT(reg_file_1_out_a), .RESULTS(alu_a_1_results),
    .OP_SEL(control_1_alu_a_op), .FLAGS(alu_a_1_flags));
  FLASH flash_1 (
    .ADDRESS(reg_file_1_pc_output), .DATA_OUT(flash_1_data_out), .CLK(control_1_clk),
    .WR(control_1_flash_wr), .DATA_IN(alu_a_1_results));
  Multiplexer #(.width(32), .disabled(0), .enable("false")) multiplexer_1 (
    .in0(alu_a_1_results), .in1(ram_stack_1_data_out), .out(multiplexer_1_out), .sel(WB_A));
  REG_FILE reg_file_1 (
    .B_INPUT(multiplexer_3_out), .A_INPUT(multiplexer_1_out), .SEL_A(decode_1_sel_a),
    .OUT_A(reg_file_1_out_a), .OUT_B(reg_file_1_out_b), .SEL_B(decode_1_sel_b), .SEL_C(decode_1_sel_c),
    .OUT_C(reg_file_1_out_c), .OUT_D(reg_file_1_out_d), .SEL_D(decode_1_sel_d), .WB_A(decode_1_wb_a),
    .WB_B(decode_1_wb_b), .WB_EQ(reg_file_1_wb_eq), .CLK(control_1_clk), .RST(control_1_rst),
    .PC_OUTPUT(reg_file_1_pc_output), .PC_INPUT(agu_bpu_1_pc_output));
  Multiplexer #(.width(32), .disabled(0), .enable("false")) multiplexer_2 (
    .in0(alu_a_1_results), .in1(reg_file_1_out_c), .out(multiplexer_2_out), .sel(not_1_out));
  ALU_B alu_b_1 (
    .RESULTS(alu_b_1_results), .OP_SEL(B_OP_S), .B_INPUT(multiplexer_2_out), .A_INPUT(reg_file_1_out_d),
    .FLAGS(B_FLAGS));
  RAM___STACK ram_stack_1 (
    .ADDRESS(alu_b_1_results), .MODE(control_1_mode), .CLK(control_1_clk), .DATA_IN(alu_a_1_results),
    .DATA_OUT(ram_stack_1_data_out), .STO(control_1_sto));
  Multiplexer #(.width(32), .disabled(0), .enable("false")) multiplexer_3 (
    .in0(alu_b_1_results), .in1(agu_bpu_1_pc_output), .out(multiplexer_3_out), .sel(WB_B));
  AGU___BPU agu_bpu_1 (
    .DATA_INPUT(reg_file_1_out_d), .ALU_B_FLAGS(B_FLAGS), .BRANCH(BRANCH), .PC_INPUT(reg_file_1_pc_output),
    .PC_OUTPUT(agu_bpu_1_pc_output));
endmodule

// FLASH ROMS
module FLASH (
  input  WR,
  input  CLK,
  input  [31:0] ADDRESS,
  input  [31:0] DATA_IN,
  output [31:0] DATA_OUT
);

  wire not_1_out, not_2_out;

  not not_1 (not_1_out, WR);
  RAM #(.addrWidth(24), .dataWidth(16), .Select("low")) FLASH_UPPER (
    .addr(ADDRESS[23:0]), .data(DATA_OUT[31:16]), .clk(CLK), .ld(not_1_out));  // open: sel, clr
  not not_2 (not_2_out, not_1_out);
  RAM #(.addrWidth(24), .dataWidth(16), .Select("low")) FLASH_LOWER (
    .addr(ADDRESS[23:0]), .data(DATA_OUT[15:0]), .clk(CLK), .ld(not_1_out));  // open: sel, clr
  assign DATA_OUT[31:16] = not_2_out ? DATA_IN[31:16] : 16'bz;  // Controlled_Buffer controlled_buffer_1
  assign DATA_OUT[15:0] = not_2_out ? DATA_IN[15:0] : 16'bz;  // Controlled_Buffer controlled_buffer_2
endmodule

module DECODE (
  input  [31:0] INSTR_IN,
  output [31:0] INSTR_OUT,
  output [4:0] WB_A,
  output [4:0] SEL_A,
  output [4:0] SEL_B,
  output [2:0] ALU_A,
  output [4:0] WB_B,
  output [4:0] SEL_C,
  output [4:0] SEL_D,
  output [2:0] ALU_B
);

  Pull_Resistor pull_resistor_1 (.node(WB_A));
  Pull_Resistor pull_resistor_2 (.node(SEL_A));
  Pull_Resistor pull_resistor_3 (.node(SEL_B));
  Pull_Resistor pull_resistor_4 (.node(INSTR_OUT));
  Pull_Resistor pull_resistor_5 (.node(ALU_A));
  Pull_Resistor pull_resistor_6 (.node(WB_B));
  Pull_Resistor pull_resistor_7 (.node(SEL_C));
  Pull_Resistor pull_resistor_8 (.node(SEL_D));
  Pull_Resistor pull_resistor_9 (.node(ALU_B));
endmodule

// CONTROL LOGIC
module CONTROL (
  input  WB_EQ,
  input  [7:0] ALU_A_FLAGS,
  input  [7:0] B_FLAGS,
  input  HALT,
  output FLASH_WR,
  output ALU_A_SEL,
  output [2:0] ALU_A_OP,
  output WB_A,
  output WB_B,
  output [2:0] B_OP_S,
  output [2:0] MODE,
  output STO,
  output BRANCH,
  output CLK,
  output RST
);

  wire clock_1_out, d_ff_1_qn;

  Pull_Resistor pull_resistor_1 (.node(FLASH_WR));
  Pull_Resistor pull_resistor_2 (.node(WB_EQ));
  Pull_Resistor pull_resistor_3 (.node(ALU_A_OP));
  Pull_Resistor pull_resistor_4 (.node(ALU_A_SEL));
  Pull_Resistor pull_resistor_5 (.node(WB_A));
  Pull_Resistor pull_resistor_6 (.node(WB_B));
  Pull_Resistor pull_resistor_7 (.node(B_OP_S));
  Pull_Resistor pull_resistor_8 (.node(MODE));
  Pull_Resistor pull_resistor_9 (.node(STO));
  Pull_Resistor pull_resistor_10 (.node(BRANCH));
  Clock clock_1 (.out(clock_1_out));
  D_Flip_Flop #(.Pre_Clr_Positions("LEGACY"), .enable("true"), .NewFFLayout("false")) d_ff_1 (
    .clk(HALT), .D(d_ff_1_qn), .Qn(d_ff_1_qn));  // open: Q, preset, en, reset
  and and_1 (CLK, clock_1_out, d_ff_1_qn);
  Pull_Resistor pull_resistor_11 (.node(RST));
  Pull_Resistor pull_resistor_12 (.node(CLK));
endmodule

module REG_FILE (
  input  [4:0] SEL_A,
  input  [4:0] WB_A,
  input  [4:0] SEL_B,
  input  [4:0] SEL_C,
  input  [4:0] WB_B,
  input  [31:0] PC_INPUT,
  input  [31:0] B_INPUT,
  input  [31:0] A_INPUT,
  input  CLK,
  input  RST,
  input  [4:0] SEL_D,
  output [31:0] OUT_A,
  output [31:0] OUT_B,
  output WB_EQ,
  output [31:0] OUT_C,
  output [31:0] PC_OUTPUT,
  output [31:0] OUT_D
);

  wire decoder_1_out0, decoder_1_out1, decoder_2_out0, decoder_2_out1, demultiplexer_1_out0,
       demultiplexer_1_out1, demultiplexer_1_out2, demultiplexer_1_out3, demultiplexer_1_out4,
       demultiplexer_1_out5, demultiplexer_1_out6, demultiplexer_1_out7, demultiplexer_1_out8,
       demultiplexer_1_out9, demultiplexer_1_out10, demultiplexer_1_out11, demultiplexer_1_out12,
       demultiplexer_1_out13, demultiplexer_1_out14, demultiplexer_1_out15, demultiplexer_2_out0,
       demultiplexer_2_out1, demultiplexer_2_out2, demultiplexer_2_out3, demultiplexer_2_out4,
       demultiplexer_2_out5, demultiplexer_2_out6, demultiplexer_2_out7, demultiplexer_2_out8,
       demultiplexer_2_out9, demultiplexer_2_out10, demultiplexer_2_out11, demultiplexer_2_out12,
       demultiplexer_2_out13, demultiplexer_2_out14, demultiplexer_2_out15, demultiplexer_3_out0,
       demultiplexer_3_out1, demultiplexer_3_out2, demultiplexer_3_out3, demultiplexer_3_out4,
       demultiplexer_3_out5, demultiplexer_3_out6, demultiplexer_3_out7, demultiplexer_3_out8,
       demultiplexer_3_out9, demultiplexer_3_out10, demultiplexer_3_out11, demultiplexer_3_out12,
       demultiplexer_3_out13, demultiplexer_3_out14, demultiplexer_3_out15, demultiplexer_4_out0,
       demultiplexer_4_out1, demultiplexer_4_out2, demultiplexer_4_out3, demultiplexer_4_out4,
       demultiplexer_4_out5, demultiplexer_4_out6, demultiplexer_4_out7, demultiplexer_4_out8,
       demultiplexer_4_out9, demultiplexer_4_out10, demultiplexer_4_out11, demultiplexer_4_out12,
       demultiplexer_4_out13, demultiplexer_4_out14, demultiplexer_4_out15, nor_1_out, or_1_out, or_2_out,
       or_3_out, or_4_out, or_5_out, or_6_out, or_7_out, or_8_out, or_9_out, or_10_out, or_11_out, or_12_out,
       or_13_out, or_14_out, or_15_out, or_16_out, or_17_out, or_18_out, or_19_out, or_20_out, or_21_out,
       or_22_out, or_23_out, or_24_out, or_25_out, or_26_out, or_27_out, or_28_out, or_29_out, or_30_out,
       undriven;
  wire [31:0] A0_q, A1_q, A2_q, A3_q, FP_q, GP_q, multiplexer_1_out, multiplexer_2_out, multiplexer_3_out,
       multiplexer_4_out, multiplexer_5_out, multiplexer_6_out, multiplexer_7_out, multiplexer_8_out,
       multiplexer_9_out, multiplexer_10_out, multiplexer_11_out, multiplexer_12_out, multiplexer_13_out,
       multiplexer_14_out, multiplexer_15_out, multiplexer_16_out, multiplexer_17_out, multiplexer_18_out,
       multiplexer_19_out, multiplexer_20_out, multiplexer_21_out, multiplexer_22_out, multiplexer_23_out,
       multiplexer_24_out, multiplexer_25_out, multiplexer_26_out, multiplexer_27_out, multiplexer_28_out,
       multiplexer_29_out, multiplexer_30_out, multiplexer_31_out, multiplexer_32_out, multiplexer_33_out,
       multiplexer_34_out, multiplexer_35_out, multiplexer_36_out, multiplexer_38_out, multiplexer_39_out,
       multiplexer_42_out, multiplexer_43_out, RA_q, S0_q, S1_q, S2_q, S3_q, S4_q, S5_q, S6_q, S7_q, SP_q,
       T0_q, T1_q, T2_q, T3_q, T4_q, T5_q, T6_q, T7_q, T8_q, T9_q, T10_q, T11_q, V0_q, V1_q;

  Demultiplexer #(.select(4), .disabled(0), .enable("false")) demultiplexer_1 (
    .out0(demultiplexer_1_out0), .out1(demultiplexer_1_out1), .out2(demultiplexer_1_out2),
    .out3(demultiplexer_1_out3), .out4(demultiplexer_1_out4), .out5(demultiplexer_1_out5),
    .out6(demultiplexer_1_out6), .out7(demultiplexer_1_out7), .out8(demultiplexer_1_out8),
    .out9(demultiplexer_1_out9), .out10(demultiplexer_1_out10), .out11(demultiplexer_1_out11),
    .out12(demultiplexer_1_out12), .out13(demultiplexer_1_out13), .out14(demultiplexer_1_out14),
    .out15(demultiplexer_1_out15), .in(decoder_1_out0), .sel(WB_A[3:0]));
  Demultiplexer #(.select(4), .disabled(0), .enable("false")) demultiplexer_2 (
    .out0(demultiplexer_2_out0), .out1(demultiplexer_2_out1), .out2(demultiplexer_2_out2),
    .out3(demultiplexer_2_out3), .out4(demultiplexer_2_out4), .out5(demultiplexer_2_out5),
    .out6(demultiplexer_2_out6), .out7(demultiplexer_2_out7), .out8(demultiplexer_2_out8),
    .out9(demultiplexer_2_out9), .out10(demultiplexer_2_out10), .out11(demultiplexer_2_out11),
    .out12(demultiplexer_2_out12), .out13(demultiplexer_2_out13), .out14(demultiplexer_2_out14),
    .out15(demultiplexer_2_out15), .in(decoder_1_out1), .sel(WB_A[3:0]));
  Decoder #(.enable("false")) decoder_1 (.out0(decoder_1_out0), .out1(decoder_1_out1), .sel(WB_A[4]));
  Decoder #(.enable("false")) decoder_2 (.out0(decoder_2_out0), .out1(decoder_2_out1), .sel(WB_B[4]));
  Demultiplexer #(.select(4), .disabled(0), .enable("false")) demultiplexer_3 (
    .out0(demultiplexer_3_out0), .out1(demultiplexer_3_out1), .out2(demultiplexer_3_out2),
    .out3(demultiplexer_3_out3), .out4(demultiplexer_3_out4), .out5(demultiplexer_3_out5),
    .out6(demultiplexer_3_out6), .out7(demultiplexer_3_out7), .out8(demultiplexer_3_out8),
    .out9(demultiplexer_3_out9), .out10(demultiplexer_3_out10), .out11(demultiplexer_3_out11),
    .out12(demultiplexer_3_out12), .out13(demultiplexer_3_out13), .out14(demultiplexer_3_out14),
    .out15(demultiplexer_3_out15), .in(decoder_2_out0), .sel(WB_B[3:0]));
  Demultiplexer #(.select(4), .disabled(0), .enable("false")) demultiplexer_4 (
    .out0(demultiplexer_4_out0), .out1(demultiplexer_4_out1), .out2(demultiplexer_4_out2),
    .out3(demultiplexer_4_out3), .out4(demultiplexer_4_out4), .out5(demultiplexer_4_out5),
    .out6(demultiplexer_4_out6), .out7(demultiplexer_4_out7), .out8(demultiplexer_4_out8),
    .out9(demultiplexer_4_out9), .out10(demultiplexer_4_out10), .out11(demultiplexer_4_out11),
    .out12(demultiplexer_4_out12), .out13(demultiplexer_4_out13), .out14(demultiplexer_4_out14),
    .out15(demultiplexer_4_out15), .in(decoder_2_out1), .sel(WB_B[3:0]));
  Comparator #(.width(5), .mode("unsigned")) comparator_1 (.a(WB_A), .b(WB_B), .eq(WB_EQ));  // open: gt, lt
  Multiplexer #(.width(32), .enable("false")) multiplexer_1 (
    .in0(B_INPUT), .in1(A_INPUT), .out(multiplexer_1_out), .sel(demultiplexer_1_out1));
  Multiplexer #(.width(32), .enable("false")) multiplexer_2 (
    .in0(B_INPUT), .in1(A_INPUT), .out(multiplexer_2_out), .sel(demultiplexer_1_out2));
  Multiplexer #(.width(32), .enable("false")) multiplexer_3 (
    .in0(B_INPUT), .in1(A_INPUT), .out(multiplexer_3_out), .sel(demultiplexer_1_out3));
  Multiplexer #(.width(32), .enable("false")) multiplexer_4 (
    .in0(B_INPUT), .in1(A_INPUT), .out(multiplexer_4_out), .sel(demultiplexer_1_out4));
  Multiplexer #(.width(32), .enable("false")) multiplexer_5 (
    .in0(B_INPUT), .in1(A_INPUT), .out(multiplexer_5_out), .sel(demultiplexer_1_out5));
  Multiplexer #(.width(32), .enable("false")) multiplexer_6 (
    .in0(B_INPUT), .in1(A_INPUT), .out(multiplexer_6_out), .sel(demultiplexer_1_out6));
  Multiplexer #(.width(32), .enable("false")) multiplexer_7 (
    .in0(B_INPUT), .in1(A_INPUT), .out(multiplexer_7_out), .sel(demultiplexer_1_out7));
  Multiplexer #(.width(32), .enable("false")) multiplexer_8 (
    .in0(multiplexer_1_out), .in1(PC_INPUT), .out(multiplexer_8_out), .sel(nor_1_out));
  nor nor_1 (nor_1_out, demultiplexer_1_out1, demultiplexer_3_out1);
  or or_1 (or_1_out, demultiplexer_1_out2, demultiplexer_3_out2);
  or or_2 (or_2_out, demultiplexer_1_out3, demultiplexer_3_out3);
  or or_3 (or_3_out, demultiplexer_1_out4, demultiplexer_3_out4);
  or or_4 (or_4_out, demultiplexer_1_out5, demultiplexer_3_out5);
  or or_5 (or_5_out, demultiplexer_1_out6, demultiplexer_3_out6);
  or or_6 (or_6_out, demultiplexer_1_out7, demultiplexer_3_out7);
  Register #(.width(32), .Select("low")) PC (.D(multiplexer_8_out), .en(undriven), .Q(PC_OUTPUT), .clk(CLK), .clr(RST));
  Register #(.width(32), .Select("low")) T0 (.D(multiplexer_2_out), .en(or_1_out), .Q(T0_q), .clk(CLK), .clr(RST));
  Register #(.width(32), .Select("low")) T1 (.D(multiplexer_3_out), .en(or_2_out), .Q(T1_q), .clk(CLK), .clr(RST));
  Register #(.width(32), .Select("low")) T2 (.D(multiplexer_4_out), .en(or_3_out), .Q(T2_q), .clk(CLK), .clr(RST));
  Register #(.width(32), .Select("low")) T3 (.D(multiplexer_5_out), .en(or_4_out), .Q(T3_q), .clk(CLK), .clr(RST));
  Register #(.width(32), .Select("low")) T4 (.D(multiplexer_6_out), .en(or_5_out), .Q(T4_q), .clk(CLK), .clr(RST));
  Register #(.width(32), .Select("low")) T5 (.D(multiplexer_7_out), .en(or_6_out), .Q(T5_q), .clk(CLK), .clr(RST));
  Multiplexer #(.width(32), .enable("false")) multiplexer_9 (
    .in0(B_INPUT), .in1(A_INPUT), .out(multiplexer_9_out), .sel(demultiplexer_1_out8));
  Multiplexer #(.width(32), .enable("false")) multiplexer_10 (
    .in0(B_INPUT), .in1(A_INPUT), .out(multiplexer_10_out), .sel(demultiplexer_1_out9));
  Multiplexer #(.width(32), .enable("false")) multiplexer_11 (
    .in0(B_INPUT), .in1(A_INPUT), .out(multiplexer_11_out), .sel(demultiplexer_1_out10));
  Multiplexer #(.width(32), .enable("false")) multiplexer_12 (
    .in0(B_INPUT), .in1(A_INPUT), .out(multiplexer_12_out), .sel(demultiplexer_1_out11));
  Multiplexer #(.width(32), .enable("false")) multiplexer_13 (
    .in0(B_INPUT), .in1(A_INPUT), .out(multiplexer_13_out), .sel(demultiplexer_1_out12));
  Multiplexer #(.width(32), .enable("false")) multiplexer_14 (
    .in0(B_INPUT), .in1(A_INPUT), .out(multiplexer_14_out), .sel(demultiplexer_1_out13));
  Multiplexer #(.width(32), .enable("false")) multiplexer_15 (
    .in0(B_INPUT), .in1(A_INPUT), .out(multiplexer_15_out), .sel(demultiplexer_1_out14));
  Multiplexer #(.width(32), .enable("false")) multiplexer_16 (
    .in0(B_INPUT), .in1(A_INPUT), .out(multiplexer_16_out), .sel(demultiplexer_1_out15));
  or or_7 (or_7_out, demultiplexer_1_out8, demultiplexer_3_out8);
  or or_8 (or_8_out, demultiplexer_1_out9, demultiplexer_3_out9);
  or or_9 (or_9_out, demultiplexer_1_out10, demultiplexer_3_out10);
  or or_10 (or_10_out, demultiplexer_1_out11, demultiplexer_3_out11);
  or or_11 (or_11_out, demultiplexer_1_out12, demultiplexer_3_out12);
  or or_12 (or_12_out, demultiplexer_1_out13, demultiplexer_3_out13);
  or or_13 (or_13_out, demultiplexer_1_out14, demultiplexer_3_out14);
  or or_14 (or_14_out, demultiplexer_1_out15, demultiplexer_3_out15);
  Register #(.width(32), .Select("low")) T6 (.D(multiplexer_9_out), .en(or_7_out), .Q(T6_q), .clk(CLK), .clr(RST));
  Register #(.width(32), .Select("low")) T7 (.D(multiplexer_10_out), .en(or_8_out), .Q(T7_q), .clk(CLK), .clr(RST));
  Register #(.width(32), .Select("low")) T8 (.D(multiplexer_11_out), .en(or_9_out), .Q(T8_q), .clk(CLK), .clr(RST));
  Register #(.width(32), .Select("low")) T9 (.D(multiplexer_12_out), .en(or_10_out), .Q(T9_q), .clk(CLK), .clr(RST));
  Register #(.width(32), .Select("low")) T10 (.D(multiplexer_13_out), .en(or_11_out), .Q(T10_q), .clk(CLK), .clr(RST));
  Register #(.width(32), .Select("low")) T11 (.D(multiplexer_14_out), .en(or_12_out), .Q(T11_q), .clk(CLK), .clr(RST));
  Register #(.width(32), .Select("low")) S0 (.D(multiplexer_15_out), .en(or_13_out), .Q(S0_q), .clk(CLK), .clr(RST));
  Register #(.width(32), .Select("low")) S1 (.D(multiplexer_16_out), .en(or_14_out), .Q(S1_q), .clk(CLK), .clr(RST));
  Multiplexer #(.width(32), .enable("false")) multiplexer_17 (
    .in0(B_INPUT), .in1(A_INPUT), .out(multiplexer_17_out), .sel(demultiplexer_2_out0));
  Multiplexer #(.width(32), .enable("false")) multiplexer_18 (
    .in0(B_INPUT), .in1(A_INPUT), .out(multiplexer_18_out), .sel(demultiplexer_2_out1));
  Multiplexer #(.width(32), .enable("false")) multiplexer_19 (
    .in0(B_INPUT), .in1(A_INPUT), .out(multiplexer_19_out), .sel(demultiplexer_2_out2));
  Multiplexer #(.width(32), .enable("false")) multiplexer_20 (
    .in0(B_INPUT), .in1(A_INPUT), .out(multiplexer_20_out), .sel(demultiplexer_2_out3));
  Multiplexer #(.width(32), .enable("false")) multiplexer_21 (
    .in0(B_INPUT), .in1(A_INPUT), .out(multiplexer_21_out), .sel(demultiplexer_2_out4));
  Multiplexer #(.width(32), .enable("false")) multiplexer_22 (
    .in0(B_INPUT), .in1(A_INPUT), .out(multiplexer_22_out), .sel(demultiplexer_2_out5));
  Multiplexer #(.width(32), .enable("false")) multiplexer_23 (
    .in0(B_INPUT), .in1(A_INPUT), .out(multiplexer_23_out), .sel(demultiplexer_2_out6));
  Multiplexer #(.width(32), .enable("false")) multiplexer_24 (
    .in0(B_INPUT), .in1(A_INPUT), .out(multiplexer_24_out), .sel(demultiplexer_2_out7));
  or or_15 (or_15_out, demultiplexer_2_out0, demultiplexer_4_out0);
  or or_16 (or_16_out, demultiplexer_2_out1, demultiplexer_4_out1);
  or or_17 (or_17_out, demultiplexer_2_out2, demultiplexer_4_out2);
  or or_18 (or_18_out, demultiplexer_2_out3, demultiplexer_4_out3);
  or or_19 (or_19_out, demultiplexer_2_out4, demultiplexer_4_out4);
  or or_20 (or_20_out, demultiplexer_2_out5, demultiplexer_4_out5);
  or or_21 (or_21_out, demultiplexer_2_out6, demultiplexer_4_out6);
  or or_22 (or_22_out, demultiplexer_2_out7, demultiplexer_4_out7);
  Register #(.width(32), .Select("low")) S2 (.D(multiplexer_17_out), .en(or_15_out), .Q(S2_q), .clk(CLK), .clr(RST));
  Register #(.width(32), .Select("low")) S3 (.D(multiplexer_18_out), .en(or_16_out), .Q(S3_q), .clk(CLK), .clr(RST));
  Register #(.width(32), .Select("low")) S4 (.D(multiplexer_19_out), .en(or_17_out), .Q(S4_q), .clk(CLK), .clr(RST));
  Register #(.width(32), .Select("low")) S5 (.D(multiplexer_20_out), .en(or_18_out), .Q(S5_q), .clk(CLK), .clr(RST));
  Register #(.width(32), .Select("low")) S6 (.D(multiplexer_21_out), .en(or_19_out), .Q(S6_q), .clk(CLK), .clr(RST));
  Register #(.width(32), .Select("low")) S7 (.D(multiplexer_22_out), .en(or_20_out), .Q(S7_q), .clk(CLK), .clr(RST));
  Register #(.width(32), .Select("low")) A0 (.D(multiplexer_23_out), .en(or_21_out), .Q(A0_q), .clk(CLK), .clr(RST));
  Register #(.width(32), .Select("low")) A1 (.D(multiplexer_24_out), .en(or_22_out), .Q(A1_q), .clk(CLK), .clr(RST));
  Multiplexer #(.width(32), .enable("false")) multiplexer_25 (
    .in0(B_INPUT), .in1(A_INPUT), .out(multiplexer_25_out), .sel(demultiplexer_2_out8));
  Multiplexer #(.width(32), .enable("false")) multiplexer_26 (
    .in0(B_INPUT), .in1(A_INPUT), .out(multiplexer_26_out), .sel(demultiplexer_2_out9));
  Multiplexer #(.width(32), .enable("false")) multiplexer_27 (
    .in0(B_INPUT), .in1(A_INPUT), .out(multiplexer_27_out), .sel(demultiplexer_2_out10));
  Multiplexer #(.width(32), .enable("false")) multiplexer_28 (
    .in0(B_INPUT), .in1(A_INPUT), .out(multiplexer_28_out), .sel(demultiplexer_2_out11));
  Multiplexer #(.width(32), .enable("false")) multiplexer_29 (
    .in0(B_INPUT), .in1(A_INPUT), .out(multiplexer_29_out), .sel(demultiplexer_2_out12));
  Multiplexer #(.width(32), .enable("false")) multiplexer_30 (
    .in0(B_INPUT), .in1(A_INPUT), .out(multiplexer_30_out), .sel(demultiplexer_2_out13));
  Multiplexer #(.width(32), .enable("false")) multiplexer_31 (
    .in0(B_INPUT), .in1(A_INPUT), .out(multiplexer_31_out), .sel(demultiplexer_2_out14));
  Multiplexer #(.width(32), .enable("false")) multiplexer_32 (
    .in0(B_INPUT), .in1(A_INPUT), .out(multiplexer_32_out), .sel(demultiplexer_2_out15));
  Register #(.width(32), .Select("low")) A2 (.D(multiplexer_25_out), .en(or_23_out), .Q(A2_q), .clk(CLK), .clr(RST));
  or or_23 (or_23_out, demultiplexer_2_out8, demultiplexer_4_out8);
  Register #(.width(32), .Select("low")) A3 (.D(multiplexer_26_out), .en(or_24_out), .Q(A3_q), .clk(CLK), .clr(RST));
  or or_24 (or_24_out, demultiplexer_2_out9, demultiplexer_4_out9);
  Register #(.width(32), .Select("low")) V0 (.D(multiplexer_27_out), .en(or_25_out), .Q(V0_q), .clk(CLK), .clr(RST));
  or or_25 (or_25_out, demultiplexer_2_out10, demultiplexer_4_out10);
  Register #(.width(32), .Select("low")) V1 (.D(multiplexer_28_out), .en(or_26_out), .Q(V1_q), .clk(CLK), .clr(RST));
  or or_26 (or_26_out, demultiplexer_2_out11, demultiplexer_4_out11);
  Register #(.width(32), .Select("low")) GP (.D(multiplexer_29_out), .en(or_27_out), .Q(GP_q), .clk(CLK), .clr(RST));
  or or_27 (or_27_out, demultiplexer_2_out12, demultiplexer_4_out12);
  Register #(.width(32), .Select("low")) SP (.D(multiplexer_30_out), .en(or_28_out), .Q(SP_q), .clk(CLK), .clr(RST));
  or or_28 (or_28_out, demultiplexer_2_out13, demultiplexer_4_out13);
  Register #(.width(32), .Select("low")) FP (.D(multiplexer_31_out), .en(or_29_out), .Q(FP_q), .clk(CLK), .clr(RST));
  or or_29 (or_29_out, demultiplexer_2_out14, demultiplexer_4_out14);
  Register #(.width(32), .Select("low")) RA (.D(multiplexer_32_out), .en(or_30_out), .Q(RA_q), .clk(CLK), .clr(RST));
  or or_30 (or_30_out, demultiplexer_2_out15, demultiplexer_4_out15);
  Multiplexer #(.select(4), .width(32), .disabled(0), .enable("false")) multiplexer_33 (
    .in0({32{1'b0}}), .in1(PC_OUTPUT), .in2(T0_q), .in3(T1_q), .in4(T2_q), .in5(T3_q), .in6(T4_q),
    .in7(T5_q), .in8(T6_q), .in9(T7_q), .in10(T8_q), .in11(T9_q), .in12(T10_q), .in13(T11_q), .in14(S0_q),
    .in15(S1_q), .out(multiplexer_33_out), .sel(SEL_A[3:0]));
  Multiplexer #(.select(4), .width(32), .disabled(0), .enable("false")) multiplexer_34 (
    .in0(S2_q), .in1(S3_q), .in2(S4_q), .in3(S5_q), .in4(S6_q), .in5(S7_q), .in6(A0_q), .in7(A1_q),
    .in8(A2_q), .in9(A3_q), .in10(V0_q), .in11(V1_q), .in12(GP_q), .in13(SP_q), .in14(FP_q), .in15(RA_q),
    .out(multiplexer_34_out), .sel(SEL_B[3:0]));
  Multiplexer #(.select(4), .width(32), .disabled(0), .enable("false")) multiplexer_35 (
    .in0({32{1'b0}}), .in1(PC_OUTPUT), .in2(T0_q), .in3(T1_q), .in4(T2_q), .in5(T3_q), .in6(T4_q),
    .in7(T5_q), .in8(T6_q), .in9(T7_q), .in10(T8_q), .in11(T9_q), .in12(T10_q), .in13(T11_q), .in14(S0_q),
    .in15(S1_q), .out(multiplexer_35_out), .sel(SEL_C[3:0]));
  Multiplexer #(.select(4), .width(32), .disabled(0), .enable("false")) multiplexer_36 (
    .in0(S2_q), .in1(S3_q), .in2(S4_q), .in3(S5_q), .in4(S6_q), .in5(S7_q), .in6(A0_q), .in7(A1_q),
    .in8(A2_q), .in9(A3_q), .in10(V0_q), .in11(V1_q), .in12(GP_q), .in13(SP_q), .in14(FP_q), .in15(RA_q),
    .out(multiplexer_36_out), .sel(SEL_D[3:0]));
  Multiplexer #(.width(32), .disabled(0), .enable("false")) multiplexer_37 (
    .in0(multiplexer_33_out), .in1(multiplexer_38_out), .out(OUT_A), .sel(SEL_A[4]));
  Multiplexer #(.select(4), .width(32), .disabled(0), .enable("false")) multiplexer_38 (
    .in0(S2_q), .in1(S3_q), .in2(S4_q), .in3(S5_q), .in4(S6_q), .in5(S7_q), .in6(A0_q), .in7(A1_q),
    .in8(A2_q), .in9(A3_q), .in10(V0_q), .in11(V1_q), .in12(GP_q), .in13(SP_q), .in14(FP_q), .in15(RA_q),
    .out(multiplexer_38_out), .sel(SEL_A[3:0]));
  Multiplexer #(.select(4), .width(32), .disabled(0), .enable("false")) multiplexer_39 (
    .in0({32{1'b0}}), .in1(PC_OUTPUT), .in2(T0_q), .in3(T1_q), .in4(T2_q), .in5(T3_q), .in6(T4_q),
    .in7(T5_q), .in8(T6_q), .in9(T7_q), .in10(T8_q), .in11(T9_q), .in12(T10_q), .in13(T11_q), .in14(S0_q),
    .in15(S1_q), .out(multiplexer_39_out), .sel(SEL_B[3:0]));
  Multiplexer #(.width(32), .disabled(0), .enable("false")) multiplexer_40 (
    .in0(multiplexer_39_out), .in1(multiplexer_34_out), .out(OUT_B), .sel(SEL_B[4]));
  Multiplexer #(.width(32), .disabled(0), .enable("false")) multiplexer_41 (
    .in0(multiplexer_35_out), .in1(multiplexer_42_out), .out(OUT_C), .sel(SEL_C[4]));
  Multiplexer #(.select(4), .width(32), .disabled(0), .enable("false")) multiplexer_42 (
    .in0(S2_q), .in1(S3_q), .in2(S4_q), .in3(S5_q), .in4(S6_q), .in5(S7_q), .in6(A0_q), .in7(A1_q),
    .in8(A2_q), .in9(A3_q), .in10(V0_q), .in11(V1_q), .in12(GP_q), .in13(SP_q), .in14(FP_q), .in15(RA_q),
    .out(multiplexer_42_out), .sel(SEL_C[3:0]));
  Multiplexer #(.select(4), .width(32), .disabled(0), .enable("false")) multiplexer_43 (
    .in0({32{1'b0}}), .in1(PC_OUTPUT), .in2(T0_q), .in3(T1_q), .in4(T2_q), .in5(T3_q), .in6(T4_q),
    .in7(T5_q), .in8(T6_q), .in9(T7_q), .in10(T8_q), .in11(T9_q), .in12(T10_q), .in13(T11_q), .in14(S0_q),
    .in15(S1_q), .out(multiplexer_43_out), .sel(SEL_D[3:0]));
  Multiplexer #(.width(32), .disabled(0), .enable("false")) multiplexer_44 (
    .in0(multiplexer_43_out), .in1(multiplexer_36_out), .out(OUT_D), .sel(SEL_D[4]));

  // Other names for the same wires on the sheet: PC_I[31:0] = PC_INPUT; PC_O[31:0] = PC_OUTPUT

  // Notes on the sheet:
  //   $ZERO
endmodule

module ALU_A (
  input  [31:0] B_INPUT,
  input  [31:0] A_INPUT,
  input  [2:0] OP_SEL,
  output [31:0] RESULTS,
  output [7:0] FLAGS
);

  wire and_1_out, OF;
  wire [31:0] adder_1_out, and_3_out, nor_1_out, shifter_1_out, shifter_2_out, shifter_3_out, xor_1_out,
       xor_2_out;
  wire [31:31] and_2_out;

  assign xor_1_out = B_INPUT ^ {32{and_2_out[31]}};  // XOR_Gate xor_1, 32 bits wide
  and and_1 (and_1_out, ~OP_SEL[2], ~OP_SEL[1]);  // AND_Gate
  and and_2 (and_2_out[31], and_1_out, OP_SEL[0]);
  Adder #(.width(32)) adder_1 (.a(A_INPUT), .b(xor_1_out), .out(adder_1_out), .cin(and_2_out[31]), .cout(OF));
  assign and_3_out = A_INPUT & B_INPUT;  // AND_Gate and_3, 32 bits wide
  assign nor_1_out = ~(A_INPUT | B_INPUT);  // NOR_Gate nor_1, 32 bits wide
  assign xor_2_out = A_INPUT ^ B_INPUT;  // XOR_Gate xor_2, 32 bits wide
  Shifter #(.width(32)) shifter_1 (.in(A_INPUT), .\dist (B_INPUT[4:0]), .out(shifter_1_out));
  Shifter #(.width(32), .shift("lr")) shifter_2 (.in(A_INPUT), .\dist (B_INPUT[4:0]), .out(shifter_2_out));
  Shifter #(.width(32), .shift("rl")) shifter_3 (.in(A_INPUT), .\dist (B_INPUT[4:0]), .out(shifter_3_out));
  Multiplexer #(.select(3), .width(32), .enable("false")) multiplexer_1 (
    .in0(adder_1_out), .in1(adder_1_out), .in2(and_3_out), .in3(nor_1_out), .in4(xor_2_out),
    .in5(shifter_1_out), .in6(shifter_2_out), .in7(shifter_3_out), .out(RESULTS), .sel(OP_SEL));
  Comparator #(.width(32), .mode("unsigned")) comparator_1 (
    .a({32{1'b0}}), .b(RESULTS), .eq(FLAGS[0]), .lt(FLAGS[1]));  // open: gt
  Comparator #(.width(32)) comparator_2 (.a({32{1'b0}}), .b(RESULTS), .eq(FLAGS[2]), .lt(FLAGS[3]));  // open: gt
  Comparator #(.width(32), .mode("unsigned")) comparator_3 (
    .a(A_INPUT), .b(B_INPUT), .eq(FLAGS[4]), .lt(FLAGS[5]));  // open: gt
  Comparator #(.width(32)) comparator_4 (.a(A_INPUT), .b(B_INPUT), .eq(FLAGS[6]), .lt(FLAGS[7]));  // open: gt

  // Notes on the sheet:
  //   ALUs A & B are the exact same, just the outer layouts have changed
endmodule

module ALU_B (
  input  [31:0] B_INPUT,
  input  [31:0] A_INPUT,
  input  [2:0] OP_SEL,
  output [31:0] RESULTS,
  output [7:0] FLAGS
);

  wire and_1_out, OF;
  wire [31:0] adder_1_out, and_3_out, nor_1_out, shifter_1_out, shifter_2_out, shifter_3_out, xor_1_out,
       xor_2_out;
  wire [31:31] and_2_out;

  assign xor_1_out = B_INPUT ^ {32{and_2_out[31]}};  // XOR_Gate xor_1, 32 bits wide
  and and_1 (and_1_out, ~OP_SEL[2], ~OP_SEL[1]);  // AND_Gate
  and and_2 (and_2_out[31], and_1_out, OP_SEL[0]);
  Adder #(.width(32)) adder_1 (.a(A_INPUT), .b(xor_1_out), .out(adder_1_out), .cin(and_2_out[31]), .cout(OF));
  assign and_3_out = A_INPUT & B_INPUT;  // AND_Gate and_3, 32 bits wide
  assign nor_1_out = ~(A_INPUT | B_INPUT);  // NOR_Gate nor_1, 32 bits wide
  assign xor_2_out = A_INPUT ^ B_INPUT;  // XOR_Gate xor_2, 32 bits wide
  Shifter #(.width(32)) shifter_1 (.in(A_INPUT), .\dist (B_INPUT[4:0]), .out(shifter_1_out));
  Shifter #(.width(32), .shift("lr")) shifter_2 (.in(A_INPUT), .\dist (B_INPUT[4:0]), .out(shifter_2_out));
  Shifter #(.width(32), .shift("rl")) shifter_3 (.in(A_INPUT), .\dist (B_INPUT[4:0]), .out(shifter_3_out));
  Multiplexer #(.select(3), .width(32), .enable("false")) multiplexer_1 (
    .in0(adder_1_out), .in1(adder_1_out), .in2(and_3_out), .in3(nor_1_out), .in4(xor_2_out),
    .in5(shifter_1_out), .in6(shifter_2_out), .in7(shifter_3_out), .out(RESULTS), .sel(OP_SEL));
  Comparator #(.width(32), .mode("unsigned")) comparator_1 (
    .a({32{1'b0}}), .b(RESULTS), .eq(FLAGS[0]), .lt(FLAGS[1]));  // open: gt
  Comparator #(.width(32)) comparator_2 (.a({32{1'b0}}), .b(RESULTS), .eq(FLAGS[2]), .lt(FLAGS[3]));  // open: gt
  Comparator #(.width(32), .mode("unsigned")) comparator_3 (
    .a(B_INPUT), .b(B_INPUT), .eq(FLAGS[4]), .lt(FLAGS[5]));  // open: gt
  Comparator #(.width(32)) comparator_4 (.a(A_INPUT), .b(B_INPUT), .eq(FLAGS[6]), .lt(FLAGS[7]));  // open: gt

  // Notes on the sheet:
  //   ALUs A & B are the exact same, just the outer layouts have changed
endmodule

module AGU___BPU (
  input  BRANCH,
  input  [7:0] ALU_B_FLAGS,
  input  [31:0] DATA_INPUT,
  input  [31:0] PC_INPUT,
  output [31:0] PC_OUTPUT
);

  Adder #(.width(32)) adder_1 (.a(PC_INPUT), .b(32'h1), .out(PC_OUTPUT));  // open: cin, cout
endmodule

module RAM___STACK (
  input  [31:0] ADDRESS,
  input  [31:0] DATA_IN,
  input  [2:0] MODE,
  input  STO,
  input  CLK,
  output [31:0] DATA_OUT
);

  wire not_1_out, pull_resistor_1_node, undriven, undriven_2, undriven_3, undriven_4, undriven_5, undriven_6,
       undriven_7, undriven_8, undriven_9, undriven_10, undriven_11;
  wire [23:0] controlled_buffer_1_out, controlled_buffer_2_out, controlled_buffer_3_out,
       controlled_buffer_4_out, controlled_buffer_5_out, controlled_buffer_6_out, controlled_buffer_7_out,
       controlled_buffer_8_out, controlled_buffer_9_out, controlled_buffer_10_out, controlled_buffer_11_out,
       controlled_buffer_12_out, multiplexer_1_out, or_1_out;

  assign controlled_buffer_1_out = undriven ? 24'hf3fe7f : 24'bz;  // Controlled_Buffer controlled_buffer_1
  assign controlled_buffer_2_out = undriven_2 ? 24'hf3fe00 : 24'bz;  // Controlled_Buffer controlled_buffer_2
  assign controlled_buffer_3_out = undriven_4 ? 24'hf40000 : 24'bz;  // Controlled_Buffer controlled_buffer_3
  assign controlled_buffer_4_out = undriven_6 ? 24'hf3fe80 : 24'bz;  // Controlled_Buffer controlled_buffer_4
  assign controlled_buffer_5_out = undriven_3 ? 24'hf5ffff : 24'bz;  // Controlled_Buffer controlled_buffer_5
  assign controlled_buffer_6_out = undriven_5 ? 24'hf3ff7f : 24'bz;  // Controlled_Buffer controlled_buffer_6
  assign controlled_buffer_7_out = undriven_7 ? 24'hf7ffff : 24'bz;  // Controlled_Buffer controlled_buffer_7
  assign controlled_buffer_8_out = undriven_8 ? 24'hf60000 : 24'bz;  // Controlled_Buffer controlled_buffer_8
  assign controlled_buffer_9_out = undriven_9 ? 24'hf3ffff : 24'bz;  // Controlled_Buffer controlled_buffer_9
  assign controlled_buffer_10_out = undriven_10 ? 24'hf3ff80 : 24'bz;  // Controlled_Buffer controlled_buffer_10
  assign controlled_buffer_11_out = pull_resistor_1_node ? 24'hf80000 : 24'bz;  // Controlled_Buffer controlled_buffer_11
  Pull_Resistor pull_resistor_1 (.node(pull_resistor_1_node));
  assign controlled_buffer_12_out = undriven_11 ? {24{1'b1}} : 24'bz;  // Controlled_Buffer controlled_buffer_12
  Multiplexer #(.select(3), .width(24), .enable("false")) multiplexer_1 (
    .in0(ADDRESS[23:0]), .in2(controlled_buffer_2_out), .in3(controlled_buffer_4_out),
    .in4(controlled_buffer_10_out), .in5(controlled_buffer_3_out), .in6(controlled_buffer_8_out),
    .in7(controlled_buffer_11_out), .out(multiplexer_1_out), .sel(MODE));  // open: in1
  assign or_1_out = multiplexer_1_out | ADDRESS[23:0];  // OR_Gate or_1, 24 bits wide
  Pull_Resistor pull_resistor_2 (.node(or_1_out));
  RAM #(.addrWidth(24), .dataWidth(32), .Select("low")) RAM___STACK (
    .addr(or_1_out), .data(DATA_OUT), .clk(CLK), .ld(not_1_out));  // open: sel, clr
  not not_1 (not_1_out, STO);
  assign DATA_OUT = STO ? DATA_IN : 32'bz;  // Controlled_Buffer controlled_buffer_13

  // Notes on the sheet:
  //   000 - LOD RAM
  //   001 - STO RAM
  //   010 - SET GP-REGS
  //   011 - SET FP-REGS
  //   100 - SET IO-REGS
  //   101 - USE GP-FIFO
  //   110 - USE GP-LIFO
  //   111 - USE FUNC LIFO
  //   RAM               : 0x000000-0xF3FDFF -> 15,990,271 words, 63.96MB~
  //   GP RAM-REGISTERS  : 0xF3FE00-0xF3FE7F -> 128        words, 512B
  //   FP RAM-REGISTERS  : 0xF3FE80-0xF3FF7F -> 256        words, 1kB
  //   IO RAM-REGISTERS  : 0xF3FF80-0xF3FFFF -> 128        words, 512B
  //   GP-FIFO QUEUE ADDR: 0xF40000-0xF5FFFF -> 131,072    words, 512kB
  //   GP-LIFO STACK ADDR: 0xF60000-0xF7FFFF -> 131,072    words, 512kB
  //   FUNC    STACK ADDR: 0xF80000-0xFFFFFF -> 65,536     words, 64kB
endmodule
